# Fritzing sketch companion (saved by Fritzing 0.9.3b)

parts:
  WeMos_D1_Mini1 = WeMos D1 Mini
  U1 = RF-LINK_TX [package=rf-link_tx]
  ANT1 = Antenna

nets:
  5V: WeMos_D1_Mini1.5V, U1.+5V
  N1: WeMos_D1_Mini1.D3, U1.DATA
  N2: WeMos_D1_Mini1.G, U1.GND
  N3: U1.ANT, ANT1.antenna_lead
